// Logisim project MiniCPU.circ as structural Verilog: 7 circuits, main circuit main
module main (
);

  wire and_1_out, and_2_out, cki_1_acpt, Clk, comparator_1_eq, comparator_1_gt, comparator_1_lt,
       control_branch_1_take, ERAM, IMM, KEY, keyboard_1_avail, or_1_out, PCC, RS, WEA, WEB, WEC, WED, WES;
  wire [2:0] OP, SRC, SRC2;
  wire [3:0] OpCode;
  wire [6:0] keyboard_1_data, multiplexer_5_out;
  wire [8:0] multiplexer_5_out_2;
  wire [15:0] A, A_q, adder_1_out, alu_1_p4, B, B_q, C_q, D_q, IMB, multiplexer_3_out, multiplexer_4_out,
       PC_q, undriven, Z_q;
  wire [19:0] rom_1_data;

  Keyboard keyboard_1 (.clk(Clk), .re(and_1_out), .avail(keyboard_1_avail), .data(keyboard_1_data));  // open: clr
  and and_1 (and_1_out, KEY, cki_1_acpt);
  CKI cki_1 (.SRC2(SRC2), .ACPT(cki_1_acpt));
  Register #(.width(16)) Z (.Q(Z_q), .clk(Clk));  // open: D, en, clr
  Register #(.width(16)) u_A (.D({multiplexer_5_out_2, multiplexer_5_out}), .en(WEA), .Q(A_q), .clk(Clk));  // open: clr
  Register #(.width(16)) u_B (.D({multiplexer_5_out_2, multiplexer_5_out}), .en(WEB), .Q(B_q), .clk(Clk));  // open: clr
  Register #(.width(16)) C (.D({multiplexer_5_out_2, multiplexer_5_out}), .en(WEC), .Q(C_q), .clk(Clk));  // open: clr
  Register #(.width(16)) D (.D({multiplexer_5_out_2, multiplexer_5_out}), .en(WED), .Q(D_q), .clk(Clk));  // open: clr
  or or_1 (or_1_out, ~and_1_out, keyboard_1_avail);  // OR_Gate
  TTY #(.rows(4), .cols(20)) tty_1 (.data(multiplexer_5_out), .clk(Clk), .we(WES));  // open: clr
  Multiplexer #(.select(3), .width(16), .enable("false")) multiplexer_1 (
    .in0(Z_q), .in1(A_q), .in2(B_q), .in3(C_q), .in4(D_q), .in5({{9{1'b0}}, keyboard_1_data}), .out(A),
    .sel(SRC));  // open: in6, in7
  Multiplexer #(.select(3), .width(16), .enable("false")) multiplexer_2 (
    .in0(Z_q), .in1(A_q), .in2(B_q), .in3(C_q), .in4(D_q), .in5({{9{1'b0}}, keyboard_1_data}), .out(B),
    .sel(SRC2));  // open: in6, in7
  Multiplexer #(.width(16), .enable("false")) multiplexer_3 (.in0(A), .in1(IMB), .out(multiplexer_3_out), .sel(IMM));
  Register #(.width(16)) PC (.D(multiplexer_4_out), .en(or_1_out), .Q(PC_q), .clk(Clk));  // open: clr
  Multiplexer #(.width(16), .enable("false")) multiplexer_4 (
    .in0(adder_1_out), .in1(IMB), .out(multiplexer_4_out), .sel(and_2_out));
  and and_2 (and_2_out, PCC, control_branch_1_take);
  Adder #(.width(16)) adder_1 (.a(PC_q), .b(16'h1), .out(adder_1_out));  // open: cin, cout
  ROM #(.addrWidth(16), .dataWidth(24)) rom_1 (
    .addr(PC_q), .data({OpCode, rom_1_data[19:17], SRC, SRC2, rom_1_data[10:0]}));
  RAM #(.addrWidth(16), .dataWidth(16)) ram_1 (.addr(alu_1_p4), .we(ERAM), .clk(Clk));  // open: oe, data
  // ALU alu_1: pin names not known; wires that end beside it: multiplexer_3_out, B, OP, alu_1_p4
  Comparator #(.width(16)) comparator_1 (
    .a(A), .b(B), .gt(comparator_1_gt), .eq(comparator_1_eq), .lt(comparator_1_lt));
  Clock clock_1 (.out(Clk));
  Control_branch control_branch_1 (
    .OpCode(OpCode), .GTR(comparator_1_gt), .EQL(comparator_1_eq), .LES(comparator_1_lt),
    .TAKE(control_branch_1_take));
  Multiplexer #(.width(16), .enable("false")) multiplexer_5 (
    .in0(undriven), .in1(alu_1_p4), .out({multiplexer_5_out_2, multiplexer_5_out}), .sel(RS));
  Control_log control_log_1 (.OpCode(OpCode), .KEY(KEY), .IMM(IMM), .ERAM(ERAM), .RS(RS), .OP(OP), .PCC(PCC));
  assign IMB = {{5{rom_1_data[10]}}, rom_1_data[10:0]};  // Bit_Extender bit_extender_1
  Control_DEST control_dest_1 (.DEST(rom_1_data[19:17]), .WEA(WEA), .WEB(WEB), .WEC(WEC), .WED(WED), .WES(WES));

  // Notes on the sheet:
  //   contents of rom_1 (hex, n*v repeats v):
  //   424000 42800 c8000 1617f6 60c008 a0892c 120801 500001 60400d 120fff 94092c c8000 500008 444000
  //   14000a c8000 500000
endmodule

module ALU (
  input  [15:0] X,
  input  [2:0] OP,
  input  [15:0] Y,
  output [15:0] R
);

  wire and_2_out, not_1_out, not_2_out;
  wire [15:0] adder_1_out, and_1_out, divider_1_out, divider_1_rem, multiplexer_1_out, multiplier_1_out,
       negator_1_out, or_1_out, xor_1_out;

  Negator #(.width(16)) negator_1 (.in(Y), .out(negator_1_out));
  Multiplexer #(.width(16), .enable("false")) multiplexer_1 (
    .in0(Y), .in1(negator_1_out), .out(multiplexer_1_out), .sel(and_2_out));
  assign and_1_out = X & Y;  // AND_Gate and_1, 16 bits wide
  assign or_1_out = X | Y;  // OR_Gate or_1, 16 bits wide
  assign xor_1_out = X ^ Y;  // XOR_Gate xor_1, 16 bits wide
  and and_2 (and_2_out, OP[0], not_1_out, not_2_out);
  Adder #(.width(16)) adder_1 (.a(X), .b(multiplexer_1_out), .out(adder_1_out));  // open: cin, cout
  Multiplier #(.width(16)) multiplier_1 (.a(X), .b(Y), .out(multiplier_1_out));  // open: cin, cout
  Divider #(.width(16)) divider_1 (.a(X), .b(Y), .out(divider_1_out), .rem(divider_1_rem));  // open: upper
  not not_1 (not_1_out, OP[1]);
  not not_2 (not_2_out, OP[2]);
  Multiplexer #(.select(3), .width(16), .enable("false")) multiplexer_2 (
    .in0(adder_1_out), .in1(adder_1_out), .in2(multiplier_1_out), .in3(divider_1_out), .in4(divider_1_rem),
    .in5(and_1_out), .in6(or_1_out), .in7(xor_1_out), .out(R), .sel(OP));

  // Notes on the sheet:
  //   ALU Operations
  //   000 - ADD (R = X + Y)
  //   001 - SUBTRACT (R = X - Y)
  //   010 - MULTIPLY (R = X * Y)
  //   011 - DIVIDE (R = X / Y)
  //   100 - MODULO (R = X % Y)
  //   101 - BITWISE AND (R = X & Y)
  //   110 - BITWISE OR (R = X | Y)
  //   111 - BITWISE XOR (R = X ^ Y)
endmodule

module Control_log (
  input  [3:0] OpCode,
  output KEY,
  output IMM,
  output ERAM,
  output RS,
  output [2:0] OP,
  output PCC
);

  wire and_1_out, and_2_out, and_3_out, and_4_out, and_6_out, and_7_out, and_8_out, and_9_out, and_10_out,
       and_11_out, and_12_out, and_13_out, and_14_out, and_15_out, and_16_out, and_17_out;

  and and_1 (and_1_out, ~OpCode[3], ~OpCode[2], ~OpCode[1], ~OpCode[0]);  // AND_Gate
  and and_2 (and_2_out, OpCode[3], ~OpCode[2], OpCode[1], OpCode[0]);  // AND_Gate
  and and_3 (and_3_out, ~OpCode[2], ~OpCode[1], OpCode[0]);  // AND_Gate
  and and_4 (and_4_out, OpCode[3], ~OpCode[2], OpCode[1], ~OpCode[0]);  // AND_Gate
  and and_5 (ERAM, OpCode[3], ~OpCode[2], OpCode[1], ~OpCode[0]);  // AND_Gate
  and and_6 (and_6_out, ~OpCode[3], ~OpCode[2]);  // AND_Gate
  and and_7 (and_7_out, ~OpCode[2], OpCode[1], OpCode[0]);  // AND_Gate
  and and_8 (and_8_out, OpCode[2], ~OpCode[1], ~OpCode[0]);  // AND_Gate
  and and_9 (and_9_out, ~OpCode[2], OpCode[1], OpCode[0]);  // AND_Gate
  and and_10 (and_10_out, OpCode[2], ~OpCode[1]);  // AND_Gate
  and and_11 (and_11_out, ~OpCode[3], OpCode[1]);  // AND_Gate
  and and_12 (and_12_out, OpCode[1], OpCode[0]);
  and and_13 (and_13_out, OpCode[3], ~OpCode[1], ~OpCode[0]);  // AND_Gate
  and and_14 (and_14_out, OpCode[3], OpCode[2]);
  and and_15 (and_15_out, ~OpCode[3], OpCode[2], OpCode[0]);  // AND_Gate
  and and_16 (and_16_out, ~OpCode[3], OpCode[2], OpCode[1]);  // AND_Gate
  and and_17 (and_17_out, OpCode[3], ~OpCode[2], ~OpCode[1], ~OpCode[0]);  // AND_Gate
  or or_1 (KEY, and_1_out, and_2_out);
  or or_2 (IMM, and_3_out, and_4_out);
  or or_3 (RS, and_6_out, and_7_out, and_8_out);
  or or_4 (OP[1], and_9_out, and_10_out);
  or or_5 (OP[0], and_11_out, and_12_out, and_13_out, and_14_out);
  or or_6 (PCC, and_15_out, and_16_out, and_17_out);

  assign OP[2] = 1'b0;
endmodule

module Control_DEST (
  input  [2:0] DEST,
  output WEA,
  output WEB,
  output WEC,
  output WED,
  output WES
);

  and and_1 (WEA, ~DEST[2], ~DEST[1], DEST[0]);  // AND_Gate
  and and_2 (WEB, ~DEST[2], DEST[1], ~DEST[0]);  // AND_Gate
  and and_3 (WEC, ~DEST[2], DEST[1], DEST[0]);  // AND_Gate
  and and_4 (WED, DEST[2], ~DEST[1], ~DEST[0]);  // AND_Gate
  and and_5 (WES, DEST[2], DEST[1], ~DEST[0]);  // AND_Gate
endmodule

module Control_branch (
  input  [3:0] OpCode,
  input  GTR,
  input  EQL,
  input  LES,
  output TAKE
);

  wire and_1_out, and_2_out, and_3_out, and_4_out;

  and and_1 (and_1_out, ~OpCode[3], OpCode[2], ~OpCode[1], OpCode[0]);  // AND_Gate
  and and_2 (and_2_out, ~OpCode[3], OpCode[2], OpCode[0], GTR, ~EQL, ~LES);  // AND_Gate
  and and_3 (and_3_out, ~OpCode[3], OpCode[2], OpCode[1], ~OpCode[0], ~GTR, EQL, ~LES);  // AND_Gate
  and and_4 (and_4_out, OpCode[3], ~OpCode[2], ~OpCode[1], ~OpCode[0], ~GTR, ~EQL, LES);  // AND_Gate
  or or_1 (TAKE, and_1_out, and_2_out, and_3_out, and_4_out);
endmodule

module Control_Keyboard_input (
  input  [2:0] SRC2,
  output ACPT
);

  and and_1 (ACPT, SRC2[2], ~SRC2[1], SRC2[0]);  // AND_Gate
endmodule

module CKI (
  input  [2:0] SRC2,
  output ACPT
);

  and and_1 (ACPT, SRC2[2], ~SRC2[1], SRC2[0]);  // AND_Gate
endmodule
